// Logisim project Unidade_Prevenção_de_Desvio.circ as structural Verilog: 1 circuit, main circuit main
module main (
  input  E,
  output _1___take
);

  wire and_1_out, and_2_out, and_3_out, and_4_out, CLK, NE, NQ0, NQ1, or_1_out, Q0;

  Clock clock_1 (.out(CLK));
  and and_1 (and_1_out, _1___take, NE);
  and and_2 (and_2_out, NQ1, Q0, E);
  and and_3 (and_3_out, _1___take, NQ0);
  or or_1 (or_1_out, and_1_out, and_2_out, and_3_out);
  not not_1 (NE, E);
  and and_4 (and_4_out, NQ0, E);
  D_Flip_Flop D1 (.clk(CLK), .D(or_1_out), .Q(_1___take), .Qn(NQ1));  // open: preset, en, reset
  D_Flip_Flop D0 (.clk(CLK), .D(and_4_out), .Q(Q0), .Qn(NQ0));  // open: preset, en, reset

  // Other names for the same wires on the sheet: Q1 = _1___take

  // Notes on the sheet:
  //   ESTADO TAKE
  //   NOT TAKE
  //   0 = Not Take
endmodule
