// Logisim project isa_8_bits.circ as structural Verilog: 9 circuits, main circuit main
module main (
);

  wire BRZR, CLK, DADO_BREG, MUX_ULA, REG_A, W_BREG, WM;
  wire [1:0] multiplexer_3_out, PC_SEL;
  wire [2:0] OP_ULA;
  wire [3:0] OPCODE, rom_1_data;
  wire [7:0] adder_1_out, IMM, multiplexer_1_out, multiplexer_2_out, multiplexer_4_out, multiplexer_5_out,
       PC_IMM, PC_q, RA, ram_1_dout, RB, ula_1_c;

  Clock clock_1 (.out(CLK));
  Multiplexer #(.width(8)) multiplexer_1 (.in0(adder_1_out), .in1(RB), .out(multiplexer_1_out), .sel(BRZR));
  Multiplexer #(.select(2), .width(8)) multiplexer_2 (
    .in0(adder_1_out), .in1(PC_IMM), .in2(multiplexer_1_out), .out(multiplexer_2_out), .sel(PC_SEL));  // open: in3
  Register PC (.D(multiplexer_2_out), .en(1'b1), .clk(CLK), .Q(PC_q));  // open: clr
  Adder adder_1 (.a(PC_q), .b(8'h1), .out(adder_1_out));  // open: cin, cout
  ROM rom_1 (.addr(PC_q), .data({OPCODE, rom_1_data}));
  Adder adder_2 (.a(PC_q), .b(IMM), .out(PC_IMM));  // open: cin, cout
  ROM #(.addrWidth(4), .dataWidth(10)) rom_2 (
    .addr(OPCODE), .data({PC_SEL, REG_A, W_BREG, MUX_ULA, DADO_BREG, WM, OP_ULA}));
  assign IMM = {{4{rom_1_data[3]}}, rom_1_data};  // Bit_Extender bit_extender_1
  Comparator comparator_1 (.a(RA), .b({8{1'b0}}), .eq(BRZR));  // open: gt, lt
  Multiplexer #(.width(2)) multiplexer_3 (.in0(rom_1_data[3:2]), .in1(2'b00), .out(multiplexer_3_out), .sel(REG_A));
  BANCO_REGISTRADORES banco_registradores_1 (
    .DADO(multiplexer_4_out), .RS1(multiplexer_3_out), .YES_NO(W_BREG), .RD(multiplexer_3_out),
    .RS2(rom_1_data[1:0]), .CLK(CLK), .A(RA), .B(RB));
  Multiplexer #(.width(8)) multiplexer_4 (.in0(ula_1_c), .in1(ram_1_dout), .out(multiplexer_4_out), .sel(DADO_BREG));
  Multiplexer #(.width(8)) multiplexer_5 (.in0(RB), .in1(IMM), .out(multiplexer_5_out), .sel(MUX_ULA));
  ULA ula_1 (.A(RA), .B(multiplexer_5_out), .OPULA(OP_ULA), .C(ula_1_c));  // open: ZERO
  RAM ram_1 (.addr(RB), .we(WM), .oe(1'b1), .clk(CLK), .din(RA), .dout(ram_1_dout));

  // Notes on the sheet:
  //   CONTROLA QUAL TIPO DE SOMA DE PC EH FEITA
  //   SE BRZR FOR 0 (RA != 0) USA PC+1, CASO CONTRARIO PC+RB
  //   FAZ ATUALIZAÇÃO PC+1
  //   contents of rom_1 (hex, n*v repeats v):
  //   44 30 24 d4 4 10
  //   FAZ PC + IMM
  //   contents of rom_2 (hex, n*v repeats v):
  //   200 100 50 8 e4 0 0 0 40 41 42 43 44 45 46 47
  //   ESCREVE NO BANCO
  //   UNIDADE DE CONTROLE
  //   RB
  //   RA
  //   OPCODE
  //   IMM
  //   VALIDA SE USA R[A] OU 0
  //   PARA ACEITAR SALTOS COM NUM NEGATIVOS (COMPLEMENTO DE 2)
  //   INSTRUÇÃO BRANCH ON ZERO
  //   CONTROLA SE ULA RECEBE R[B] OU IMM
  //   CONTROLA QUAL O DADO QUE VAI SER ENTRADA DA PORTA DE ESCRITA DO BREG SE USA OU MEM
  //   OPCODE DA ULA
  //   REGISTRADOR B EH O QUE INTERESSA PARA LOAD E STORE
  //   constante 1 ali serve para dizer que ali na saida temos o que recebemos como entrada
  //   O QUE VAI SER ESCRITO EM MEMORIA EH O QUE ESTA NO RA
  //   CONTROLA SE ESCREVE OU NÃO NA MEMÓRIA
endmodule

module BANCO_REGISTRADORES (
  input  [7:0] DADO,
  input  [1:0] RS1,
  input  YES_NO,
  input  [1:0] RD,
  input  [1:0] RS2,
  input  CLK,
  output [7:0] A,
  output [7:0] B
);

  wire demultiplexer_1_out0, demultiplexer_1_out1, demultiplexer_1_out2, demultiplexer_1_out3;
  wire [7:0] multiplexer_1_out, multiplexer_2_out, multiplexer_3_out, multiplexer_4_out, R0_q, R1_q, R2_q,
       R3_q;

  Demultiplexer #(.select(2)) demultiplexer_1 (
    .out0(demultiplexer_1_out0), .out1(demultiplexer_1_out1), .out2(demultiplexer_1_out2),
    .out3(demultiplexer_1_out3), .in(YES_NO), .sel(RD));
  Multiplexer #(.width(8)) multiplexer_1 (.in0(R0_q), .in1(DADO), .out(multiplexer_1_out), .sel(demultiplexer_1_out0));
  Multiplexer #(.width(8)) multiplexer_2 (.in0(R1_q), .in1(DADO), .out(multiplexer_2_out), .sel(demultiplexer_1_out1));
  Multiplexer #(.width(8)) multiplexer_3 (.in0(R2_q), .in1(DADO), .out(multiplexer_3_out), .sel(demultiplexer_1_out2));
  Multiplexer #(.width(8)) multiplexer_4 (.in0(R3_q), .in1(DADO), .out(multiplexer_4_out), .sel(demultiplexer_1_out3));
  Register R0 (.D(multiplexer_1_out), .clk(CLK), .Q(R0_q));  // open: en, clr
  Register R1 (.D(multiplexer_2_out), .clk(CLK), .Q(R1_q));  // open: en, clr
  Register R2 (.D(multiplexer_3_out), .clk(CLK), .Q(R2_q));  // open: en, clr
  Register R3 (.D(multiplexer_4_out), .clk(CLK), .Q(R3_q));  // open: en, clr
  Multiplexer #(.select(2), .width(8)) multiplexer_5 (
    .in0(R0_q), .in1(R1_q), .in2(R2_q), .in3(R3_q), .out(A), .sel(RS1));
  Multiplexer #(.select(2), .width(8)) multiplexer_6 (
    .in0(R0_q), .in1(R1_q), .in2(R2_q), .in3(R3_q), .out(B), .sel(RS2));
endmodule

module ULA (
  input  [7:0] A,
  input  [7:0] B,
  input  [2:0] OPULA,
  output ZERO,
  output [7:0] C
);

  wire [7:0] adder_1_out, and_1_out, not_1_out, or_1_out, shifter_1_out, shifter_2_out, subtractor_1_out,
       xor_1_out;

  assign not_1_out = ~B;  // NOT_Gate not_1, 8 bits wide
  assign and_1_out = A & B;  // AND_Gate and_1, 8 bits wide
  assign or_1_out = A | B;  // OR_Gate or_1, 8 bits wide
  assign xor_1_out = A ^ B;  // XOR_Gate xor_1, 8 bits wide
  Adder adder_1 (.a(A), .b(B), .out(adder_1_out));  // open: cin, cout
  Subtractor subtractor_1 (.a(A), .b(B), .out(subtractor_1_out));  // open: bin, bout
  Shifter shifter_1 (.in(A), .\dist (B[2:0]), .out(shifter_1_out));
  Shifter #(.shift("lr")) shifter_2 (.in(A), .\dist (B[2:0]), .out(shifter_2_out));
  Multiplexer #(.select(3), .width(8)) multiplexer_1 (
    .in0(not_1_out), .in1(and_1_out), .in2(or_1_out), .in3(xor_1_out), .in4(adder_1_out),
    .in5(subtractor_1_out), .in6(shifter_1_out), .in7(shifter_2_out), .out(C), .sel(OPULA));
  Comparator comparator_1 (.a({8{1'b0}}), .b(C), .eq(ZERO));  // open: gt, lt

  // Notes on the sheet:
  //   NOT
  //   AND
  //   OR
  //   XOR
  //   SOMADOR
  //   SUBTRATOR
  //   SHIFT_LEFT
  //   SHIFT_LEFT
endmodule

module main_pipeline (
);

  wire A_OU_0, and_1_out, BRANCH_TAKEN, BRZR, CLK, DADO_BREG, ESCREVE_OU_NAO_IF_ID, FLUSH_EX_MEM,
       FLUSH_ID_EX, FLUSH_MEM_WB, hazard_unit_1_pc_write, MUX_ULA, not_1_out, ula_1_zero, W_BREG, WM;
  wire [1:0] ex_mem_1_rd_out, FWD_A, FWD_B, id_ex_1_rd_out, PC_SEL, PC_SEL_EX, RD, RS1_EX, RS1_IN, RS2_EX,
       RS2_IN;
  wire [2:0] OP_ULA;
  wire [3:0] OPCODE;
  wire [7:0] adder_1_out, ALU_OUT, ESCREVE_BREG, ex_mem_1_store_out, id_ex_1_a_out, id_ex_1_b_out,
       id_ex_1_imm_out, IMM, mem_wb_1_alu_out, mem_wb_1_mem_out, multiplexer_1_out, multiplexer_2_out,
       multiplexer_4_out, multiplexer_5_out, multiplexer_6_out, PC_IMM, PC_OUT, ram_1_dout, REG_A, REG_B,
       register_1_q, rom_1_data, ula_1_c, undriven;
  wire [9:0] CONTROL_ID;

  Clock clock_1 (.out(CLK));
  Multiplexer #(.select(2), .width(8)) multiplexer_1 (
    .in0(adder_1_out), .in1(PC_IMM), .in2(multiplexer_2_out), .out(multiplexer_1_out), .sel(PC_SEL_EX));  // open: in3
  Multiplexer #(.width(8)) multiplexer_2 (.in0(adder_1_out), .in1(REG_B), .out(multiplexer_2_out), .sel(BRZR));
  Register register_1 (.D(multiplexer_1_out), .en(hazard_unit_1_pc_write), .clk(CLK), .Q(register_1_q));  // open: clr
  Adder adder_1 (.a(register_1_q), .b(8'h1), .out(adder_1_out));  // open: cin, cout
  ROM rom_1 (.addr(register_1_q), .data(rom_1_data));
  Adder adder_2 (.a(PC_OUT), .b(IMM), .out(PC_IMM));  // open: cin, cout
  IF_ID if_id_1 (
    .PC_IN(register_1_q), .INSTRU_IN(rom_1_data), .ESCREVE_OU_NAO(ESCREVE_OU_NAO_IF_ID), .CLOCK(CLK),
    .PC_OUT(PC_OUT), .INSTRU_OUT({OPCODE, RS1_IN, RS2_IN}));
  Comparator comparator_1 (.a(REG_A), .b({8{1'b0}}), .eq(BRZR));  // open: gt, lt
  ROM #(.addrWidth(4), .dataWidth(10)) rom_2 (.addr(OPCODE), .data(CONTROL_ID));
  assign IMM = {{4{RS1_IN[1]}}, {RS1_IN, RS2_IN}};  // Bit_Extender bit_extender_1
  Multiplexer #(.width(2)) multiplexer_3 (.in0(RS1_IN), .in1(2'b00), .out(RD), .sel(A_OU_0));
  BANCO_REGISTRADORES banco_registradores_1 (
    .DADO(ESCREVE_BREG), .RS1(RD), .YES_NO(W_BREG), .RD(RD), .RS2(RS2_IN), .CLK(CLK), .A(REG_A), .B(REG_B));
  and and_1 (and_1_out, not_1_out, DADO_BREG);
  not not_1 (not_1_out, WM);
  HAZARD_UNIT hazard_unit_1 (
    .RD_EX(id_ex_1_rd_out), .RS1_ID(RS1_IN), .RS2_ID(RS2_IN), .ZERO_EX(ula_1_zero), .BRZ_EX(BRZR),
    .LOAD_EX(and_1_out), .PC_SEL_UC(PC_SEL), .PC_WRITE(hazard_unit_1_pc_write),
    .IF_ID_WRITE(ESCREVE_OU_NAO_IF_ID), .FLUSH_ID_EX(FLUSH_ID_EX), .FLUSH_EX_MEM(FLUSH_EX_MEM),
    .FLUSH_MEM_WB(FLUSH_MEM_WB), .BRANCH_TAKEN_EX(BRANCH_TAKEN), .PC_SEL_EX(PC_SEL_EX));  // open: HAZ_LOAD
  ID_EX id_ex_1 (
    .RS1_IN(RS1_IN), .RS2_IN(RS2_IN), .A_IN(REG_A), .B_IN(REG_B), .IMM_IN(IMM), .CONTROL_IN(CONTROL_ID),
    .FLUSH(FLUSH_ID_EX), .RD_IN(RD), .CLK(CLK), .ESCREVE_OU_NAO(1'b1), .RS1_OUT(RS1_EX), .RS2_OUT(RS2_EX),
    .A_OUT(id_ex_1_a_out), .B_OUT(id_ex_1_b_out), .IMM_OUT(id_ex_1_imm_out),
    .CONTROL_OUT({PC_SEL, A_OU_0, W_BREG, MUX_ULA, DADO_BREG, WM, OP_ULA}), .RD_OUT(id_ex_1_rd_out));
  Multiplexer #(.select(2), .width(8)) multiplexer_4 (
    .in0(id_ex_1_a_out), .in1(ALU_OUT), .in2(ESCREVE_BREG), .out(multiplexer_4_out), .sel(FWD_A));  // open: in3
  Multiplexer #(.width(8)) multiplexer_5 (
    .in0(id_ex_1_b_out), .in1(id_ex_1_imm_out), .out(multiplexer_5_out), .sel(MUX_ULA));
  Multiplexer #(.select(2), .width(8)) multiplexer_6 (
    .in0(undriven), .in1(ALU_OUT), .in2(ESCREVE_BREG), .out(multiplexer_6_out), .sel(FWD_B));  // open: in3
  ULA ula_1 (.A(multiplexer_4_out), .B(multiplexer_5_out), .OPULA(OP_ULA), .ZERO(ula_1_zero), .C(ula_1_c));
  EX_MEM ex_mem_1 (
    .ALU_IN(ula_1_c), .STORE_IN(id_ex_1_a_out),
    .CONTROL_IN({PC_SEL, A_OU_0, W_BREG, MUX_ULA, DADO_BREG, WM, OP_ULA}), .RD_IN(id_ex_1_rd_out), .CLK(CLK),
    .ESCREVE_OU_NAO(1'b1), .FLUSH(FLUSH_EX_MEM), .ALU_OUT(ALU_OUT), .STORE_OUT(ex_mem_1_store_out),
    .CONTROL_OUT({PC_SEL, A_OU_0, W_BREG, MUX_ULA, DADO_BREG, WM, OP_ULA}), .RD_OUT(ex_mem_1_rd_out));
  RAM ram_1 (.addr(ALU_OUT), .we(WM), .oe(1'b1), .clk(CLK), .din(ex_mem_1_store_out), .dout(ram_1_dout));
  MEM_WB mem_wb_1 (
    .MEM_IN(ram_1_dout), .ALU_IN(ALU_OUT),
    .CONTROL_IN({PC_SEL, A_OU_0, W_BREG, MUX_ULA, DADO_BREG, WM, OP_ULA}), .RD_IN(ex_mem_1_rd_out),
    .FLUSH(FLUSH_MEM_WB), .CLK(CLK), .ESCREVE_OU_NAO(1'b1), .MEM_OUT(mem_wb_1_mem_out),
    .ALU_OUT(mem_wb_1_alu_out), .CONTROL_OUT({PC_SEL, A_OU_0, W_BREG, MUX_ULA, DADO_BREG, WM, OP_ULA}),
    .RD_OUT(RD));
  Multiplexer #(.width(8)) multiplexer_7 (
    .in0(mem_wb_1_alu_out), .in1(mem_wb_1_mem_out), .out(ESCREVE_BREG), .sel(DADO_BREG));

  // Other names for the same wires on the sheet: WM_EX = WM; DADO_BREG_EX = DADO_BREG

  // Notes on the sheet:
  //   SE BRZR FOR 0 (RA != 0) USA PC+1, CASO CONTRARIO PC+RB
  //   CONTROLA QUAL TIPO DE SOMA DE PC EH FEITA
  //   FAZ ATUALIZAÇÃO PC+1
  //   contents of rom_1 (hex, n*v repeats v):
  //   6*44
  //   FAZ PC + IMM
  //   RB
  //   RA
  //   OPCODE
  //   contents of rom_2 (hex, n*v repeats v):
  //   200 100 50 8 e4 0 0 0 40 41 42 43 44 45 46 47
  //   UNIDADE DE CONTROLE
  //   INSTRUÇÃO BRANCH ON ZERO
endmodule

module IF_ID (
  input  [7:0] PC_IN,
  input  [7:0] INSTRU_IN,
  input  ESCREVE_OU_NAO,
  input  CLOCK,
  output [7:0] PC_OUT,
  output [7:0] INSTRU_OUT
);

  Register PC_REG (.D(PC_IN), .en(ESCREVE_OU_NAO), .clk(CLOCK), .Q(PC_OUT));  // open: clr
  Register IR_REG (.D(INSTRU_IN), .en(ESCREVE_OU_NAO), .clk(CLOCK), .Q(INSTRU_OUT));  // open: clr
endmodule

module ID_EX (
  input  [1:0] RS1_IN,
  input  [1:0] RS2_IN,
  input  [7:0] A_IN,
  input  [7:0] B_IN,
  input  [7:0] IMM_IN,
  input  [9:0] CONTROL_IN,
  input  FLUSH,
  input  [1:0] RD_IN,
  input  CLK,
  input  ESCREVE_OU_NAO,
  output [1:0] RS1_OUT,
  output [1:0] RS2_OUT,
  output [7:0] A_OUT,
  output [7:0] B_OUT,
  output [7:0] IMM_OUT,
  output [9:0] CONTROL_OUT,
  output [1:0] RD_OUT
);

  wire [9:0] multiplexer_1_out;

  Multiplexer #(.width(10)) multiplexer_1 (.in0(CONTROL_IN), .in1({10{1'b0}}), .out(multiplexer_1_out), .sel(FLUSH));
  Register #(.width(2)) RS1_REG (.D(RS1_IN), .Q(RS1_OUT));  // open: en, clk, clr
  Register #(.width(2)) RS2_REG (.D(RS2_IN), .Q(RS2_OUT));  // open: en, clk, clr
  Register A_REG (.D(A_IN), .en(ESCREVE_OU_NAO), .clk(CLK), .Q(A_OUT));  // open: clr
  Register B_REG (.D(B_IN), .en(ESCREVE_OU_NAO), .clk(CLK), .Q(B_OUT));  // open: clr
  Register IMM_REG (.D(IMM_IN), .en(ESCREVE_OU_NAO), .clk(CLK), .Q(IMM_OUT));  // open: clr
  Register #(.width(10)) CTRL_REG (
    .D(multiplexer_1_out), .en(ESCREVE_OU_NAO), .clk(CLK), .Q(CONTROL_OUT));  // open: clr
  Register #(.width(2)) RD_REG (.D(RD_IN), .en(ESCREVE_OU_NAO), .clk(CLK), .Q(RD_OUT));  // open: clr
endmodule

module EX_MEM (
  input  [7:0] ALU_IN,
  input  [7:0] STORE_IN,
  input  [9:0] CONTROL_IN,
  input  [1:0] RD_IN,
  input  CLK,
  input  ESCREVE_OU_NAO,
  input  FLUSH,
  output [7:0] ALU_OUT,
  output [7:0] STORE_OUT,
  output [9:0] CONTROL_OUT,
  output [1:0] RD_OUT
);

  wire [9:0] multiplexer_1_out;

  Multiplexer #(.width(10)) multiplexer_1 (.in0(CONTROL_IN), .in1({10{1'b0}}), .out(multiplexer_1_out), .sel(FLUSH));
  Register ALU_REG (.D(ALU_IN), .en(ESCREVE_OU_NAO), .clk(CLK), .Q(ALU_OUT));  // open: clr
  Register STORE_REG (.D(STORE_IN), .en(ESCREVE_OU_NAO), .clk(CLK), .Q(STORE_OUT));  // open: clr
  Register #(.width(10)) CTRL_REG (
    .D(multiplexer_1_out), .en(ESCREVE_OU_NAO), .clk(CLK), .Q(CONTROL_OUT));  // open: clr
  Register #(.width(2)) RD_REG (.D(RD_IN), .en(ESCREVE_OU_NAO), .clk(CLK), .Q(RD_OUT));  // open: clr
endmodule

module MEM_WB (
  input  [7:0] MEM_IN,
  input  [7:0] ALU_IN,
  input  [9:0] CONTROL_IN,
  input  [1:0] RD_IN,
  input  FLUSH,
  input  CLK,
  input  ESCREVE_OU_NAO,
  output [7:0] MEM_OUT,
  output [7:0] ALU_OUT,
  output [9:0] CONTROL_OUT,
  output [1:0] RD_OUT
);

  wire [9:0] multiplexer_1_out;

  Multiplexer #(.width(10)) multiplexer_1 (.in0(CONTROL_IN), .in1({10{1'b0}}), .out(multiplexer_1_out), .sel(FLUSH));
  Register MEM_REG (.D(MEM_IN), .en(ESCREVE_OU_NAO), .clk(CLK), .Q(MEM_OUT));  // open: clr
  Register ALU_REG (.D(ALU_IN), .en(ESCREVE_OU_NAO), .clk(CLK), .Q(ALU_OUT));  // open: clr
  Register #(.width(10)) CTRL_REG (
    .D(multiplexer_1_out), .en(ESCREVE_OU_NAO), .clk(CLK), .Q(CONTROL_OUT));  // open: clr
  Register #(.width(2)) RD_REG (.D(RD_IN), .en(ESCREVE_OU_NAO), .clk(CLK), .Q(RD_OUT));  // open: clr
endmodule

module HAZARD_UNIT (
  input  [1:0] RD_EX,
  input  [1:0] RS1_ID,
  input  [1:0] RS2_ID,
  input  ZERO_EX,
  input  BRZ_EX,
  input  LOAD_EX,
  input  [1:0] PC_SEL_UC,
  output HAZ_LOAD,
  output PC_WRITE,
  output IF_ID_WRITE,
  output FLUSH_ID_EX,
  output FLUSH_EX_MEM,
  output FLUSH_MEM_WB,
  output BRANCH_TAKEN_EX,
  output [1:0] PC_SEL_EX
);

  wire comparator_1_eq, comparator_2_eq, or_1_out;

  Comparator #(.width(2)) comparator_1 (.a(RD_EX), .b(RS1_ID), .eq(comparator_1_eq));  // open: gt, lt
  Comparator #(.width(2)) comparator_2 (.a(RD_EX), .b(RS2_ID), .eq(comparator_2_eq));  // open: gt, lt
  and and_1 (BRANCH_TAKEN_EX, ZERO_EX, BRZ_EX);
  Multiplexer #(.width(2)) multiplexer_1 (.in0(PC_SEL_UC), .in1(2'b01), .out(PC_SEL_EX), .sel(BRANCH_TAKEN_EX));
  or or_1 (or_1_out, comparator_1_eq, comparator_2_eq);
  or or_2 (FLUSH_ID_EX, HAZ_LOAD, BRANCH_TAKEN_EX);
  and and_2 (HAZ_LOAD, or_1_out, LOAD_EX);
  not not_1 (IF_ID_WRITE, HAZ_LOAD);

  assign FLUSH_EX_MEM = 1'b0;
  assign FLUSH_MEM_WB = 1'b0;
  assign PC_WRITE = IF_ID_WRITE;
endmodule
